# Fritzing sketch távolság _mérő1 (1) (saved by Fritzing 0.9.9b)
breadboards: 1

parts:
  7SEG1 = 7-Segment LED I2C Backpack (blue)
  Mod1 = Raspberry Pi 4B
  HC-SR04_Sensor_1 = HC-SR04 Ultrasonic Distance Sensor
  R1 = Resistor [tolerance=±5% power=0.25 resistance=220 package=THT]
  R3 = Resistor [tolerance=±5% power=0.25 resistance=220 package=THT]
  R4 = Resistor [tolerance=±5% power=0.25 resistance=220 package=THT]
  S1 = Pushbutton [package="[THT]"]
  R2 = Resistor [tolerance=±5% power=0.25 resistance=220 package=THT]

nets:
  5V: 7SEG1.V+, Mod1.5V, HC-SR04_Sensor_1.VCC
  GND: 7SEG1.GND, Mod1.GND, HC-SR04_Sensor_1.GND, R1.Pin_1, S1.Pin_1, S1.Pin_2
  N1: 7SEG1.SDA, Mod1.GPIO2
  N2: 7SEG1.SCL, Mod1.GPIO3
  N3: Mod1.3V3, R3.Pin_0
  N4: Mod1.GPIO23, HC-SR04_Sensor_1.TRIG
  N5: Mod1.GPIO24, R1.Pin_0, R2.Pin_0
  N6: Mod1.GPIO12, R4.Pin_0
  N7: HC-SR04_Sensor_1.ECHO, R2.Pin_1
  N8: R3.Pin_1, R4.Pin_1, S1.Pin_3, S1.Pin_4

custom parts:
  7-Segment LED I2C Backpack (blue): 4-digit, 7-segment LED Display with I2C Control
